# Fritzing sketch GY-39_LCD (saved by Fritzing 0.9.3b)

parts:
  元件1 = Arduino Nano (Rev3.0)
  LCD1 = LCD screen
  R1 = Rotary Potentiometer (Large) [maximum_resistance=100kΩ package=THT]
  元件2 = GY-39 [part_number=SEN-10621]

nets:
  N1: 元件1.D1/TX, 元件2.RX
  N2: 元件1.D0/RX, 元件2.TX
  N3: 元件1.D2, LCD1.DB7
  N4: 元件1.D3, LCD1.DB6
  N5: 元件1.D4, LCD1.DB5
  N6: 元件1.D5, LCD1.DB4
  N7: 元件1.D11/MOSI, LCD1.E
  N8: 元件1.D12/MISO, LCD1.RS
  GND: 元件1.GND, LCD1.VSS, LCD1.R/W, R1.leg2, 元件2.GND
  5V: 元件1.5V, LCD1.VDD, R1.leg1
  3V3: 元件1.3V3, 元件2.VCC
  N9: LCD1.V0, R1.wiper

custom parts:
  GY-39: GY-39 based on SparkFun RPI-1031 Tilt-a-Whirl Breakout
