# Fritzing sketch GY-39_OLED (saved by Fritzing 0.9.3b)

parts:
  元件1 = Arduino Pro Mini v13
  元件2 = GY-39 [part_number=SEN-10621]
  元件3 = OLED Monochrome 128x64 1.3 inch [part_number=938]

nets:
  N1: 元件1.A4, 元件3.MOSI_SDA
  N2: 元件1.A5, 元件3.SCLK_SCK
  VCC: 元件1.VCC, 元件2.VCC, 元件3.3.3V
  GND: 元件1.GND, 元件2.GND, 元件3.GND
  N3: 元件1.D1/RX, 元件2.TX
  N4: 元件1.D0/TX, 元件2.RX

custom parts:
  GY-39: GY-39 based on SparkFun RPI-1031 Tilt-a-Whirl Breakout
  OLED Monochrome 128x64 1.3 inch: These displays are small, only about 1.3" diagonal, but very readable due to the high contrast of an OLED display. This display is made of 128x64 individual white OLED pixels, each one is turned on or off by the controller chip. Because the display makes its own light, no backlight is required. This reduces the power required to run the OLED and is why the display has such high contrast; we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
